# Fritzing sketch schematic (saved by Fritzing 0.9.3b)
breadboards: 1

parts:
  Part1 = Arduino Uno (Rev3)
  U1 = NodeMCU V1.0

nets:
  N1: Part1.D1/TX, U1.RX
  N2: Part1.RESET, U1.RST
  3V3: Part1.3V3, U1.3V3
  GND: Part1.GND, U1.GND

custom parts:
  NodeMCU V1.0: ESP8266 based NodeMCU
