# Fritzing sketch home-automation-model (saved by Fritzing 0.9.3b)
breadboards: 1

parts:
  Raspberry_Pi_1 = Raspberry Pi 3 [part_number=RPI-3-V1.2]  # not connected
  U1 = NodeMCU V1.0
  VCC1 = Battery block 9V
  WeMos_D1_Mini_Relay_Shield_V1 = WeMos D1 Mini Relay Shield V2
  LED1 = LEDs [package=led10mm]

nets:
  N1: U1.D0, WeMos_D1_Mini_Relay_Shield_V1.D0
  N2: U1.GND, VCC1.-, WeMos_D1_Mini_Relay_Shield_V1.G
  VIN: U1.Vin, VCC1.+, WeMos_D1_Mini_Relay_Shield_V1.5V
  N3: WeMos_D1_Mini_Relay_Shield_V1.COM, LED1.A
  N4: WeMos_D1_Mini_Relay_Shield_V1.NO, LED1.C

notes:
  Power supply for the ESP8266 might as well occur through:
  - A USB port
  - A supply regulator connected to a battery
  - A Wall Wart
  - A 9v battery
  - A 3.3V regulator

custom parts:
  NodeMCU V1.0: ESP8266 based NodeMCU
